# Fritzing sketch schema_platine (saved by Fritzing 0.9.3b)
breadboards: 1

parts:
  Composant1 = Arduino Nano (Rev3.0)
  Composant3 = LED Matrix - Serial Interface - Red/Green/Blue  # not connected
  Composant2 = LED Matrix - Serial Interface - Red/Green/Blue
  Composant4 = LED Matrix - Serial Interface - Red/Green/Blue  # not connected
  Composant5 = LED Matrix - Serial Interface - Red/Green/Blue  # not connected
  Composant6 = Bluetooth HC-05 Macho
  Composant7 = Real Time Clock Module - DS1307 RTC Breakout Board

nets:
  N1: Composant1.GND, Composant2.SCK
  N2: Composant1.D11/MOSI, Composant2.MOSI
  N3: Composant1.D12/MISO, Composant2.GND
  VIN: Composant1.VIN, Composant2.VCC
  5V: Composant1.5V, Composant6.VCC, Composant7.5V
  N4: Composant1.D13/SCK, Composant2.CS

notes:
  GND
  VCC
  DIN
  CS
  CLK
